# Fritzing sketch Schema (saved by Fritzing 0.9.3b)

parts:
  Raspberry_Pi_1 = Raspberry Pi 3 [part_number=RPI-3-V1.2]
  S1 = H-Bridge with L298N
  M1 = DC Motor
  M2 = DC Motor
  VCC1 = Battery
  U1 = 2-Channel 5v Relay Shield [package=relay-2ch5v10a]
  VCC2 = 4 x AAA Battery Mount

nets:
  N1: Raspberry_Pi_1.GPIO2, U1.IN1
  N2: Raspberry_Pi_1.GPIO21, S1.ENA, S1.ENA-5V
  N3: Raspberry_Pi_1.GPIO20, S1.IN1
  GND: Raspberry_Pi_1.GPIO16, Raspberry_Pi_1.GND, Raspberry_Pi_1.GPIO23, S1.GND, S1.IN2, S1.IN3, U1.GND, VCC2.-
  N4: Raspberry_Pi_1.GPIO24, S1.IN4
  N5: Raspberry_Pi_1.GPIO18, Raspberry_Pi_1.GPIO15, S1.ENB
  5V: Raspberry_Pi_1.5V, U1.VCC
  N6: S1.12V, U1.K1-On
  N7: S1.M1-01, M2.pin_2
  N8: S1.M1-02, M2.pin_1
  N9: S1.M2-01, M1.pin_2
  N10: S1.M2-02, M1.pin_1
  N11: VCC1.+, U1.K1-In

custom parts:
  H-Bridge with L298N: h-bridge
  2-Channel 5v Relay Shield: 2 Channel 5v Relay Shield w. 2x SPD-06VDC-SD-C
